# Fritzing sketch tilt-sensor (saved by Fritzing 0.9.3b)
breadboards: 1

parts:
  Part1 = Arduino Uno (Rev3)
  S1 = Tilt Switch [package=THT]
  S2 = Tilt Switch [package=THT]
  R1 = Resistor [tolerance=±5% resistance=10k package=THT]
  R2 = Resistor [tolerance=±5% resistance=10k package=THT]

nets:
  N1: Part1.D8, S2.Pin_2, R1.Pin_1
  N2: Part1.D7, S1.Pin_2, R2.Pin_1
  N3: Part1.5V, R1.Pin_0, R2.Pin_0
  N4: Part1.GND, S1.Pin_1, S2.Pin_1
